# Fritzing sketch lab2_12led_breadboard_2 (saved by Fritzing 0.9.3b)
breadboards: 1

parts:
  Part1 = Arduino Uno (Rev3)
  R1 = Resistor [tolerance=±5% resistance=220 package=THT]
  LED1 = LED - 5mm [color="Red (633nm)" package="5 mm [THT]"]
  LED2 = LED - 5mm [color="Red (633nm)" package="5 mm [THT]"]
  LED3 = LED - 5mm [color="Red (633nm)" package="5 mm [THT]"]
  LED4 = LED - 5mm [color="Red (633nm)" package="5 mm [THT]"]
  LED5 = LED - 5mm [color="Red (633nm)" package="5 mm [THT]"]
  LED6 = LED - 5mm [color="Red (633nm)" package="5 mm [THT]"]
  R2 = Resistor [tolerance=±5% resistance=220 package=THT]
  LED7 = LED - 5mm [color="Red (633nm)" package="5 mm [THT]"]
  LED8 = LED - 5mm [color="Red (633nm)" package="5 mm [THT]"]
  LED9 = LED - 5mm [color="Red (633nm)" package="5 mm [THT]"]
  LED10 = LED - 5mm [color="Red (633nm)" package="5 mm [THT]"]
  LED11 = LED - 5mm [color="Red (633nm)" package="5 mm [THT]"]
  LED12 = LED - 5mm [color="Red (633nm)" package="5 mm [THT]"]
  R3 = Resistor [tolerance=±5% resistance=220 package=THT]
  R4 = Resistor [tolerance=±5% resistance=220 package=THT]
  R5 = Resistor [tolerance=±5% resistance=220 package=THT]
  R6 = Resistor [tolerance=±5% resistance=220 package=THT]
  R7 = Resistor [tolerance=±5% resistance=220 package=THT]
  R8 = Resistor [tolerance=±5% resistance=220 package=THT]
  R9 = Resistor [tolerance=±5% resistance=220 package=THT]
  R10 = Resistor [tolerance=±5% resistance=220 package=THT]
  R11 = Resistor [tolerance=±5% resistance=220 package=THT]
  R12 = Resistor [tolerance=±5% resistance=220 package=THT]

nets:
  N1: Part1.D8, R8.Pin_0
  N2: Part1.D9_PWM, R6.Pin_0
  N3: Part1.D10_PWM/SS, R3.Pin_0
  N4: Part1.D11_PWM/MOSI, R4.Pin_0
  N5: Part1.D12/MISO, R2.Pin_0
  N6: Part1.D13/SCK, R1.Pin_0
  N7: Part1.GND, LED1.cathode, LED2.cathode, LED3.cathode, LED4.cathode, LED5.cathode, LED6.cathode, LED7.cathode, LED8.cathode, LED9.cathode, LED10.cathode, LED11.cathode, LED12.cathode
  N8: Part1.D2, R11.Pin_0
  N9: Part1.D3_PWM, R9.Pin_0
  N10: Part1.D4, R12.Pin_0
  N11: Part1.D5_PWM, R10.Pin_0
  N12: Part1.D6_PWM, R7.Pin_0
  N13: Part1.D7, R5.Pin_0
  N14: R1.Pin_1, LED1.anode
  N15: LED2.anode, R2.Pin_1
  N16: LED3.anode, R4.Pin_1
  N17: LED4.anode, R3.Pin_1
  N18: LED5.anode, R6.Pin_1
  N19: LED6.anode, R8.Pin_1
  N20: LED7.anode, R12.Pin_1
  N21: LED8.anode, R5.Pin_1
  N22: LED9.anode, R9.Pin_1
  N23: LED10.anode, R11.Pin_1
  N24: LED11.anode, R10.Pin_1
  N25: LED12.anode, R7.Pin_1

notes:
  Longer leg connects to resistor, shorter leg to ground.
